// Digital circuit Processor.dig as structural Verilog
module Processor (
);

  wire acc, acc_op, acc_opx, acc_opy, ALU_flags, ALU_ready, branch, clk, DM_val, done, en_write, flags,
       instr_in, load, load_x, load_y, move, pop, push, \reg , reg_file_1_p4, reg_file_1_p18, reg_file_1_p19,
       reset, reset_cu, rez, sign_extend_1_p2, SP, stall, start, store, str_rez, x, y;
  wire [9:0] reg_file_1_p5;

  // reg_file reg_file_1: pin names not known; wires that end beside it: stall, branch, reset_cu, reg_file_1_p4, reg_file_1_p5, push, pop, ALU_ready, ALU_flags, rez, str_rez, acc_opx, acc_opy, load_x, load_y, DM_val, clk, reg_file_1_p18, reg_file_1_p19, reg_file_1_p5[0], reg_file_1_p5[1], reg_file_1_p5[9:2], SP, flags, acc, x, y, \reg 
  // IM im_1: pin names not known; wires that end beside it: en_write, instr_in, reg_file_1_p18, clk, reg_file_1_p4
  // Sign_extend sign_extend_1: pin names not known; wires that end beside it: reg_file_1_p5[9:2], sign_extend_1_p2
  // Control_Unit control_unit_1: pin names not known; wires that end beside it: reg_file_1_p19, reg_file_1_p5[0], ALU_ready, start, flags, reset, clk, move, store, branch, pop, push, stall, str_rez, acc_op, load_y, load_x, acc_opx, acc_opy, done, reset_cu
  // ALU alu_1: pin names not known; wires that end beside it: reg_file_1_p19, sign_extend_1_p2, \reg , reset_cu, store, move, clk, ALU_ready, ALU_flags, rez
  // DM dm_1: pin names not known; wires that end beside it: rez, load, store, push, pop, reg_file_1_p5[9:1], SP, DM_val
endmodule
